// Logisim project project3.circ as structural Verilog: 2 circuits, main circuit main
// T0
module main (
  input  in_1,
  output [15:0] out_2
);

  wire and_1_out, and_2_out, and_3_out, and_4_out, and_5_out, and_6_out, and_7_out, and_8_out, and_9_out,
       and_10_out, and_11_out, and_12_out, and_13_out, clock_1_out, D0_LD, D1_ST, D2_MOV, D3_PSH, D4_PUL,
       D5_ADD, D6_SUB, D7_DEC, D8_INC, D9_AND, D10_OR, D11_NOT, D12_LSL, D13_LSR, D14_BRA, D15_BEQ, D16_BNE,
       D17_CALL, D18_RET, decoder_4_out0, decoder_4_out1, decoder_4_out2, IR_EN, IR_LH, MEM_CLR, MEM_LD,
       MEM_SEL, MEM_STR, MuxCSel, not_1_out, not_2_out, not_3_out, not_4_out, not_5_out, or_1_out, or_2_out,
       SCR, T0, T1, T2, T3, T4, T5, T6, T7;
  wire [1:0] _3RB_FS, _4RB_FS, controlled_buffer_1_out, controlled_buffer_9_out, controlled_buffer_36_out,
       controlled_buffer_38_out, controlled_buffer_53_out, IR_FS, MuxASel, MuxBSel, OutASel, OutBSel,
       OutCSel, OutDSel;
  wire [3:0] _3RB_RS, _4RB_RS, ALUFS;

  counter counter_1 (
    .out_2(T0), .out_3(T1), .out_4(T2), .out_5(T3), .out_6(T4), .out_7(T5), .out_8(T6), .out_9(T7), .in_1(SCR));
  and and_1 (and_1_out, D0_LD, out_2[8], T3);
  assign controlled_buffer_1_out = and_1_out ? out_2[10:9] : 2'bz;  // Controlled_Buffer controlled_buffer_1
  assign OutDSel = and_1_out ? 2'b01 : 2'bz;  // Controlled_Buffer controlled_buffer_2
  assign MuxASel = and_1_out ? 2'b01 : 2'bz;  // Controlled_Buffer controlled_buffer_3
  assign _4RB_FS = and_1_out ? 2'b01 : 2'bz;  // Controlled_Buffer controlled_buffer_4
  not not_1 (not_1_out, out_2[10]);
  and and_2 (and_2_out, D2_MOV, T3, not_1_out, not_2_out);
  assign OutASel = and_2_out ? out_2[6:5] : 2'bz;  // Controlled_Buffer controlled_buffer_5
  assign MuxCSel = and_2_out ? 1'b1 : 1'bz;  // Controlled_Buffer controlled_buffer_6
  assign ALUFS = and_2_out ? 4'b0000 : 4'bz;  // Controlled_Buffer controlled_buffer_7
  assign MuxASel = and_2_out ? 2'b11 : 2'bz;  // Controlled_Buffer controlled_buffer_8
  Decoder #(.select(2)) decoder_1 (
    .out0(_4RB_RS[0]), .out1(_4RB_RS[1]), .out2(_4RB_RS[2]), .out3(_4RB_RS[3]),
    .sel(controlled_buffer_9_out), .en(and_2_out));
  assign controlled_buffer_9_out = and_2_out ? out_2[9:8] : 2'bz;  // Controlled_Buffer controlled_buffer_9
  assign _4RB_FS = and_2_out ? 2'b01 : 2'bz;  // Controlled_Buffer controlled_buffer_10
  assign MEM_SEL = T0 ? 1'b1 : 1'bz;  // Controlled_Buffer controlled_buffer_11
  assign MEM_LD = T0 ? 1'b1 : 1'bz;  // Controlled_Buffer controlled_buffer_12
  assign _3RB_FS = T0 ? 2'b10 : 2'bz;  // Controlled_Buffer controlled_buffer_13
  assign _3RB_RS = T0 ? 4'b0001 : 4'bz;  // Controlled_Buffer controlled_buffer_14
  assign IR_EN = T0 ? 1'b1 : 1'bz;  // Controlled_Buffer controlled_buffer_15
  assign IR_FS = T0 ? 2'b11 : 2'bz;  // Controlled_Buffer controlled_buffer_16
  assign IR_LH = T0 ? 1'b0 : 1'bz;  // Controlled_Buffer controlled_buffer_17
  assign MEM_STR = T0 ? 1'b0 : 1'bz;  // Controlled_Buffer controlled_buffer_18
  assign OutDSel = T0 ? 2'b00 : 2'bz;  // Controlled_Buffer controlled_buffer_19
  assign MEM_CLR = T0 ? 1'b0 : 1'bz;  // Controlled_Buffer controlled_buffer_20
  Decoder #(.select(5), .enable("false")) decoder_2 (
    .out0(D0_LD), .out1(D1_ST), .out2(D2_MOV), .out3(D3_PSH), .out4(D4_PUL), .out5(D5_ADD), .out6(D6_SUB),
    .out7(D7_DEC), .out8(D8_INC), .out9(D9_AND), .out10(D10_OR), .out11(D11_NOT), .out12(D12_LSL),
    .out13(D13_LSR), .out14(D14_BRA), .out15(D15_BEQ), .out16(D16_BNE), .out17(D17_CALL), .out18(D18_RET),
    .sel(out_2[15:11]));  // open: out19, out20, out21, out22, out23, out24, out25, out26, out27, out28, out29, out30, out31
  Decoder #(.select(2)) decoder_3 (
    .out0(_4RB_RS[0]), .out1(_4RB_RS[1]), .out2(_4RB_RS[2]), .out3(_4RB_RS[3]),
    .sel(controlled_buffer_1_out), .en(and_1_out));
  not not_2 (not_2_out, out_2[7]);
  assign IR_LH = T1 ? 1'b1 : 1'bz;  // Controlled_Buffer controlled_buffer_21
  assign _3RB_RS = T1 ? 4'b0001 : 4'bz;  // Controlled_Buffer controlled_buffer_22
  assign OutDSel = T1 ? 2'b00 : 2'bz;  // Controlled_Buffer controlled_buffer_23
  assign MEM_SEL = T1 ? 1'b1 : 1'bz;  // Controlled_Buffer controlled_buffer_24
  assign MEM_LD = T1 ? 1'b1 : 1'bz;  // Controlled_Buffer controlled_buffer_25
  assign IR_EN = T1 ? 1'b1 : 1'bz;  // Controlled_Buffer controlled_buffer_26
  assign IR_FS = T1 ? 2'b11 : 2'bz;  // Controlled_Buffer controlled_buffer_27
  assign _3RB_FS = T1 ? 2'b10 : 2'bz;  // Controlled_Buffer controlled_buffer_28
  assign MEM_STR = T1 ? 1'b0 : 1'bz;  // Controlled_Buffer controlled_buffer_29
  assign MEM_CLR = T1 ? 1'b0 : 1'bz;  // Controlled_Buffer controlled_buffer_30
  and and_3 (and_3_out, D2_MOV, T3, out_2[10], out_2[7]);
  assign OutCSel = and_3_out ? out_2[6:5] : 2'bz;  // Controlled_Buffer controlled_buffer_31
  assign MuxASel = and_3_out ? 2'b10 : 2'bz;  // Controlled_Buffer controlled_buffer_32
  assign MuxCSel = and_3_out ? 1'b0 : 1'bz;  // Controlled_Buffer controlled_buffer_33
  assign ALUFS = and_3_out ? 4'b0000 : 4'bz;  // Controlled_Buffer controlled_buffer_34
  assign MuxBSel = and_3_out ? 2'b11 : 2'bz;  // Controlled_Buffer controlled_buffer_35
  assign controlled_buffer_36_out = and_3_out ? out_2[9:8] : 2'bz;  // Controlled_Buffer controlled_buffer_36
  assign _3RB_FS = and_3_out ? 2'b01 : 2'bz;  // Controlled_Buffer controlled_buffer_37
  not not_3 (not_3_out, out_2[8]);
  and and_4 (and_4_out, D0_LD, not_3_out, T3);
  assign controlled_buffer_38_out = and_4_out ? out_2[10:9] : 2'bz;  // Controlled_Buffer controlled_buffer_38
  assign MuxASel = and_4_out ? 2'b00 : 2'bz;  // Controlled_Buffer controlled_buffer_39
  assign _4RB_FS = and_4_out ? 2'b01 : 2'bz;  // Controlled_Buffer controlled_buffer_40
  Decoder #(.select(2), .disabled(0)) decoder_4 (
    .out0(decoder_4_out0), .out1(decoder_4_out1), .out2(decoder_4_out2), .out3(decoder_4_out2),
    .sel(controlled_buffer_36_out), .en(and_3_out));
  assign IR_EN = T2 ? 1'b0 : 1'bz;  // Controlled_Buffer controlled_buffer_41
  Decoder #(.select(2)) decoder_5 (
    .out0(_4RB_RS[0]), .out1(_4RB_RS[1]), .out2(_4RB_RS[2]), .out3(_4RB_RS[3]),
    .sel(controlled_buffer_38_out), .en(and_4_out));
  assign _3RB_RS = decoder_4_out2 ? 4'b0010 : 4'bz;  // Controlled_Buffer controlled_buffer_42
  assign _3RB_RS = decoder_4_out2 ? 4'b0001 : 4'bz;  // Controlled_Buffer controlled_buffer_43
  assign _3RB_RS = decoder_4_out1 ? 4'b0000 : 4'bz;  // Controlled_Buffer controlled_buffer_44
  assign _3RB_RS = decoder_4_out0 ? 4'b0000 : 4'bz;  // Controlled_Buffer controlled_buffer_45
  assign MEM_SEL = D0_LD ? 1'b1 : 1'bz;  // Controlled_Buffer controlled_buffer_46
  assign MEM_LD = D0_LD ? 1'b1 : 1'bz;  // Controlled_Buffer controlled_buffer_47
  assign MEM_STR = D0_LD ? 1'b0 : 1'bz;  // Controlled_Buffer controlled_buffer_48
  assign MEM_SEL = D2_MOV ? 1'b0 : 1'bz;  // Controlled_Buffer controlled_buffer_49
  assign MEM_LD = D2_MOV ? 1'b0 : 1'bz;  // Controlled_Buffer controlled_buffer_50
  assign MEM_STR = D2_MOV ? 1'b0 : 1'bz;  // Controlled_Buffer controlled_buffer_51
  and and_5 (and_5_out, D0_LD, T4);
  assign SCR = and_5_out ? 1'b1 : 1'bz;  // Controlled_Buffer controlled_buffer_52
  Clock clock_1 (.out(clock_1_out));
  part2_main main_1 (
    .OutASel(OutASel), .OutBSel(OutBSel), .FunSel_2(_4RB_FS), .RegSel(_4RB_RS), .MuxASel(MuxASel),
    .OutCSel(OutCSel), .OutDSel(OutDSel), .FunSel_3(_3RB_FS), .RegSel_2(_3RB_RS), .L_H(IR_LH),
    .Enable(IR_EN), .FunSel_4(IR_FS), .MuxCSel(MuxCSel), .MuxBSel(MuxBSel), .FunSel(ALUFS), .in_10(MEM_STR),
    .in_11(MEM_SEL), .in_12(MEM_LD), .in_13(MEM_CLR), .out_23(out_2), .in_2(clock_1_out));  // open: out_21, out_22
  and and_6 (and_6_out, D1_ST, out_2[8], T3);
  Decoder #(.select(2)) decoder_6 (
    .out0(_4RB_RS[0]), .out1(_4RB_RS[1]), .out2(_4RB_RS[2]), .out3(_4RB_RS[3]),
    .sel(controlled_buffer_53_out), .en(and_6_out));
  assign controlled_buffer_53_out = and_6_out ? out_2[10:9] : 2'bz;  // Controlled_Buffer controlled_buffer_53
  assign OutBSel = and_6_out ? out_2[10:9] : 2'bz;  // Controlled_Buffer controlled_buffer_54
  assign ALUFS = and_6_out ? 4'b0000 : 4'bz;  // Controlled_Buffer controlled_buffer_55
  assign OutDSel = and_6_out ? 2'b01 : 2'bz;  // Controlled_Buffer controlled_buffer_56
  Hex_Digit_Display hex_digit_display_1 (.value(out_2[15:12]));  // open: dp
  Hex_Digit_Display hex_digit_display_2 (.value(out_2[11:8]));  // open: dp
  assign MEM_SEL = D1_ST ? 1'b1 : 1'bz;  // Controlled_Buffer controlled_buffer_57
  assign MEM_LD = D1_ST ? 1'b1 : 1'bz;  // Controlled_Buffer controlled_buffer_58
  assign MEM_STR = D1_ST ? 1'b1 : 1'bz;  // Controlled_Buffer controlled_buffer_59
  Hex_Digit_Display hex_digit_display_3 (.value(out_2[7:4]));  // open: dp
  Hex_Digit_Display hex_digit_display_4 (.value(out_2[3:0]));  // open: dp
  and and_7 (and_7_out, D1_ST, T4);
  assign SCR = and_7_out ? 1'b1 : 1'bz;  // Controlled_Buffer controlled_buffer_60
  or or_1 (or_1_out, out_2[2], out_2[3], out_2[4]);
  and and_8 (and_8_out, D5_ADD, T2, out_2[7]);
  not not_4 (not_4_out, or_1_out);
  and and_9 (and_9_out, and_8_out, or_1_out);
  and and_10 (and_10_out, and_8_out, not_4_out);
  assign MuxASel = and_10_out ? 2'b10 : 2'bz;  // Controlled_Buffer controlled_buffer_61
  assign _4RB_FS = and_10_out ? 2'b01 : 2'bz;  // Controlled_Buffer controlled_buffer_62
  assign _4RB_RS = and_10_out ? 4'b0010 : 4'bz;  // Controlled_Buffer controlled_buffer_63
  assign OutCSel = and_10_out ? out_2[6:5] : 2'bz;  // Controlled_Buffer controlled_buffer_64
  assign OutASel = and_10_out ? 2'b10 : 2'bz;  // Controlled_Buffer controlled_buffer_65
  assign MuxASel = and_9_out ? 2'b10 : 2'bz;  // Controlled_Buffer controlled_buffer_66
  assign _4RB_FS = and_9_out ? 2'b01 : 2'bz;  // Controlled_Buffer controlled_buffer_67
  assign OutCSel = and_9_out ? out_2[6:5] : 2'bz;  // Controlled_Buffer controlled_buffer_68
  assign _4RB_RS = and_9_out ? 4'b0001 : 4'bz;  // Controlled_Buffer controlled_buffer_69
  assign OutASel = and_9_out ? 2'b01 : 2'bz;  // Controlled_Buffer controlled_buffer_70
  and and_11 (and_11_out, D5_ADD, T3, out_2[4]);
  or or_2 (or_2_out, out_2[2], out_2[3], out_2[4]);
  not not_5 (not_5_out, or_2_out);
  and and_12 (and_12_out, and_11_out, or_2_out);
  and and_13 (and_13_out, and_11_out, not_5_out);
  assign MuxASel = and_13_out ? 2'b10 : 2'bz;  // Controlled_Buffer controlled_buffer_71
  assign _4RB_FS = and_13_out ? 2'b01 : 2'bz;  // Controlled_Buffer controlled_buffer_72
  assign _4RB_RS = and_13_out ? 4'b0010 : 4'bz;  // Controlled_Buffer controlled_buffer_73
  assign OutCSel = and_13_out ? out_2[6:5] : 2'bz;  // Controlled_Buffer controlled_buffer_74
  assign OutASel = and_13_out ? 2'b10 : 2'bz;  // Controlled_Buffer controlled_buffer_75
  assign MuxASel = and_12_out ? 2'b10 : 2'bz;  // Controlled_Buffer controlled_buffer_76
  assign _4RB_FS = and_12_out ? 2'b01 : 2'bz;  // Controlled_Buffer controlled_buffer_77
  assign OutCSel = and_12_out ? out_2[6:5] : 2'bz;  // Controlled_Buffer controlled_buffer_78
  assign _4RB_RS = and_12_out ? 4'b0001 : 4'bz;  // Controlled_Buffer controlled_buffer_79
  assign OutASel = and_12_out ? 2'b01 : 2'bz;  // Controlled_Buffer controlled_buffer_80

  // Other names for the same wires on the sheet: ADDRESS[7:0] = out_2[7:0]; INSTR[15:0] = out_2;
  //   SRCREG2[2:0] = out_2[4:2]; SRCREG1[2:0] = out_2[7:5]; AdrMOD = out_2[8]; DESTREG[2:0] = out_2[10:8];
  //   REGSEL[1:0] = out_2[10:9]; OPCODE[4:0] = out_2[15:11]

  // Notes on the sheet:
  //   MOV
  //   LD
  //   ST
  //   ADD
endmodule

module counter (
  input  in_1,
  output out_2,
  output out_3,
  output out_4,
  output out_5,
  output out_6,
  output out_7,
  output out_8,
  output out_9
);

  wire clock_1_out;
  wire [2:0] counter_1_q;

  Counter #(.width(3), .max('h7)) counter_1 (
    .Q(counter_1_q), .clk(clock_1_out), .clr(in_1));  // open: load, D, count, carry
  Clock clock_1 (.out(clock_1_out));
  Decoder #(.select(3), .enable("false")) decoder_1 (
    .out0(out_2), .out1(out_3), .out2(out_4), .out3(out_5), .out4(out_6), .out5(out_7), .out6(out_8),
    .out7(out_9), .sel(counter_1_q));
endmodule
